# Fritzing sketch energia (saved by Fritzing 0.9.4)

parts:
  Part1 = Arduino Uno (Rev3) - ICSP
  Part2 = Current Sensor 5A
  Raspberry_Pi_1 = Raspberry Pi 3 [part_number=RPI-3-V1.2]
  LED1 = LEDs [package=led10mm]
  R1 = Resistor [tolerance=±5% resistance=470 package="2512 [SMD]"]
  R2 = Resistor [tolerance=±5% resistance=220 package="2512 [SMD]"]
  U1 = MOC3031-M [package=dil06]
  U2 = TRIAC [package=to-92]
  R3 = Resistor [tolerance=±5% resistance=470 package="2512 [SMD]"]

nets:
  N1: Part1.A0, Part2.2, Part2.OUT, R1.Pin_1, U2.M1
  N2: Part1.ICSP_MISO, Part1.D12/MISO, Raspberry_Pi_1.GIPO9
  N3: Part1.D11_PWM/MOSI, Raspberry_Pi_1.GIPO10
  N4: Part1.D13/SCK, Raspberry_Pi_1.GIPO11
  GND: Part1.GND, Part2.GND, Raspberry_Pi_1.GND, U1.2
  5V: Part1.5V, Part2.VCC
  N5: Part2.1, LED1.A
  N6: Raspberry_Pi_1.GIPO5, R2.Pin_0
  N7: LED1.C, U2.G, R3.Pin_1
  N8: R1.Pin_0, U1.4, U2.M2
  N9: R2.Pin_1, U1.1
  N10: U1.6, R3.Pin_0

custom parts:
  LEDs: LEDs Standard schematic elements and footprints for 5mm, 3mm, 1206, and 0603 sized LEDs. 5mm - Spark Fun Electronics SKU : COM-00529 (and others)
